// Logisim project ex4.circ as structural Verilog: 5 circuits, main circuit RotRight
module RotRight (
  input  [15:0] INPUT0,
  input  [3:0] AMOUNT,
  output [15:0] OUTPUT0
);

  wire [15:0] TUN1OUT, TUN2IN, TUN2OUT, TUN3IN, TUN3OUT, TUN4IN, TUN4OUT;

  Multiplexer #(.enable("false"), .width(16)) multiplexer_1 (
    .in0(INPUT0), .in1(TUN1OUT), .out(TUN2IN), .sel(AMOUNT[0]));
  Multiplexer #(.enable("false"), .width(16)) multiplexer_2 (
    .in0(TUN2IN), .in1(TUN2OUT), .out(TUN3IN), .sel(AMOUNT[1]));
  rot1 rot1_1 (.out_2(TUN1OUT), .in_1(INPUT0));
  rot2 rot2_1 (.out_2(TUN2OUT), .in_1(TUN2IN));
  rot4 rot4_1 (.out_2(TUN3OUT), .in_1(TUN3IN));
  rot8 rot8_1 (.out_2(TUN4OUT), .in_1(TUN4IN));
  Multiplexer #(.enable("false"), .width(16)) multiplexer_3 (
    .in0(TUN3IN), .in1(TUN3OUT), .out(TUN4IN), .sel(AMOUNT[2]));
  Multiplexer #(.enable("false"), .width(16)) multiplexer_4 (
    .in0(TUN4IN), .in1(TUN4OUT), .out(OUTPUT0), .sel(AMOUNT[3]));

  // Other names for the same wires on the sheet: TUN1IN[15:0] = INPUT0
endmodule

module rot1 (
  input  [15:0] in_1,
  output [15:0] out_2
);


  assign out_2 = {in_1[0], in_1[15:1]};
endmodule

module rot2 (
  input  [15:0] in_1,
  output [15:0] out_2
);


  assign out_2 = {in_1[1:0], in_1[15:2]};
endmodule

module rot4 (
  input  [15:0] in_1,
  output [15:0] out_2
);


  assign out_2 = {in_1[3:0], in_1[15:4]};
endmodule

module rot8 (
  input  [15:0] in_1,
  output [15:0] out_2
);


  assign out_2 = {in_1[7:0], in_1[15:8]};
endmodule
